// Logisim project F3_Sequence_summation_circuit.circ as structural Verilog: 1 circuit, main circuit main
module main (
  input  WE,
  output [7:0] S
);

  wire CLK_out, R_out;
  wire [7:0] A_q, adder_1_out, adder_2_out;

  Adder adder_1 (.a(A_q), .b(8'h1), .out(adder_1_out));  // open: cin, cout
  Button CLK (.out(CLK_out));
  Button R (.out(R_out));
  Register A (.D(adder_1_out), .en(WE), .clk(CLK_out), .Q(A_q), .clr(R_out));
  Adder adder_2 (.a(S), .b(A_q), .out(adder_2_out));  // open: cin, cout
  Register B (.D(adder_2_out), .en(WE), .clk(CLK_out), .Q(S), .clr(R_out));
endmodule
